// Logisim project minirv.circ as structural Verilog: 1 circuit, main circuit main
module main (
);

  wire clock_1_out, clock_2_out, decoder_1_out1, decoder_1_out2, decoder_1_out3, decoder_1_out4,
       decoder_1_out5, decoder_1_out6, decoder_1_out7, decoder_1_out8, decoder_1_out9, decoder_1_out10,
       decoder_1_out11, decoder_1_out12, decoder_1_out13, decoder_1_out14, decoder_1_out15, reset;
  wire [3:0] rd_selector;
  wire [31:0] register_1_q, register_2_q, register_3_q, register_4_q, register_5_q, register_6_q,
       register_7_q, register_8_q, register_9_q, register_10_q, register_11_q, register_12_q, register_13_q,
       register_14_q, register_15_q, register_16_q, write_data;

  Counter #(.max('hffff), .width(16)) PC_counter (.clk(reset));  // open: clr, load, up, count, D, carry, Q
  Clock clock_1 (.out(clock_1_out));
  Decoder #(.select(4)) decoder_1 (
    .out1(decoder_1_out1), .out2(decoder_1_out2), .out3(decoder_1_out3), .out4(decoder_1_out4),
    .out5(decoder_1_out5), .out6(decoder_1_out6), .out7(decoder_1_out7), .out8(decoder_1_out8),
    .out9(decoder_1_out9), .out10(decoder_1_out10), .out11(decoder_1_out11), .out12(decoder_1_out12),
    .out13(decoder_1_out13), .out14(decoder_1_out14), .out15(decoder_1_out15), .sel(rd_selector));  // open: out0, en
  Button reset_button (.out(reset));
  Register #(.width(32)) register_1 (
    .D(write_data), .en(decoder_1_out1), .clk(clock_1_out), .Q(register_1_q), .clr(1'b1));
  Register #(.width(32)) register_2 (
    .D(write_data), .en(decoder_1_out8), .clk(clock_1_out), .Q(register_2_q), .clr(reset));
  Register #(.width(32)) register_3 (
    .D(write_data), .en(decoder_1_out1), .clk(clock_1_out), .Q(register_3_q), .clr(reset));
  Register #(.width(32)) register_4 (
    .D(write_data), .en(decoder_1_out9), .clk(clock_1_out), .Q(register_4_q), .clr(reset));
  Register #(.width(32)) register_5 (
    .D(write_data), .en(decoder_1_out2), .clk(clock_1_out), .Q(register_5_q), .clr(reset));
  Register #(.width(32)) register_6 (
    .D(write_data), .en(decoder_1_out10), .clk(clock_1_out), .Q(register_6_q), .clr(reset));
  Register #(.width(32)) register_7 (
    .D(write_data), .en(decoder_1_out3), .clk(clock_1_out), .Q(register_7_q), .clr(reset));
  Register #(.width(32)) register_8 (
    .D(write_data), .en(decoder_1_out11), .clk(clock_1_out), .Q(register_8_q), .clr(reset));
  RAM #(.addrWidth(16), .asyncread("true"), .byteenables("byteEnables"), .dataWidth(32), .\type ("nonvolatile")) ram_1 (.clk(clock_2_out));  // open: addr, we, oe, din, dout, be3, be2, be1, be0
  Clock clock_2 (.out(clock_2_out));
  Register #(.width(32)) register_9 (
    .D(write_data), .en(decoder_1_out4), .clk(clock_1_out), .Q(register_9_q), .clr(reset));
  Register #(.width(32)) register_10 (
    .D(write_data), .en(decoder_1_out12), .clk(clock_1_out), .Q(register_10_q), .clr(reset));
  Register #(.width(32)) register_11 (
    .D(write_data), .en(decoder_1_out5), .clk(clock_1_out), .Q(register_11_q), .clr(reset));
  Register #(.width(32)) register_12 (
    .D(write_data), .en(decoder_1_out13), .clk(clock_1_out), .Q(register_12_q), .clr(reset));
  Register #(.width(32)) register_13 (
    .D(write_data), .en(decoder_1_out6), .clk(clock_1_out), .Q(register_13_q), .clr(reset));
  Register #(.width(32)) register_14 (
    .D(write_data), .en(decoder_1_out14), .clk(clock_1_out), .Q(register_14_q), .clr(reset));
  Register #(.width(32)) register_15 (
    .D(write_data), .en(decoder_1_out7), .clk(clock_1_out), .Q(register_15_q), .clr(reset));
  Register #(.width(32)) register_16 (
    .D(write_data), .en(decoder_1_out15), .clk(clock_1_out), .Q(register_16_q), .clr(reset));
  Multiplexer #(.select(4), .width(32)) multiplexer_1 (
    .in0(register_1_q), .in1(register_3_q), .in2(register_5_q), .in3(register_7_q), .in4(register_9_q),
    .in5(register_11_q), .in6(register_13_q), .in7(register_15_q), .in8(register_2_q), .in9(register_4_q),
    .in10(register_6_q), .in11(register_8_q), .in12(register_10_q), .in13(register_12_q),
    .in14(register_14_q), .in15(register_16_q));  // open: out, sel
  Multiplexer #(.select(4), .width(32)) multiplexer_2 (
    .in0(register_1_q), .in1(register_3_q), .in2(register_5_q), .in3(register_7_q), .in4(register_9_q),
    .in5(register_11_q), .in6(register_13_q), .in7(register_15_q), .in8(register_2_q), .in9(register_4_q),
    .in10(register_6_q), .in11(register_8_q), .in12(register_10_q), .in13(register_12_q),
    .in14(register_14_q), .in15(register_16_q));  // open: out, sel
endmodule
